// Logisim project Problem 10.circ as structural Verilog: 1 circuit, main circuit main
module main (
  input  X,
  input  Y,
  input  Z,
  output C
);

  wire and_1_out, and_2_out;

  and and_1 (and_1_out, X, Y);
  and and_2 (and_2_out, X, Z);
  or or_1 (C, and_1_out, and_2_out);
endmodule
