// Logisim project Problem 8.circ as structural Verilog: 1 circuit, main circuit main
module main (
  input  A,
  input  B,
  input  C,
  output B_2,
  output G,
  output R
);

  wire AB_out, AC_prime_out, BC_out, BC_prime_out, not_1_out;

  not not_1 (not_1_out, C);
  and AB (AB_out, A, B);
  and AC_prime (AC_prime_out, A, not_1_out);
  and BC (BC_out, B, C);
  and BC_prime (BC_prime_out, B, not_1_out);
  or u_B (B_2, AB_out, BC_out);
  or u_R (R, AB_out, AC_prime_out, BC_prime_out);

  assign G = C;
endmodule
