// Logisim project Problem 9.circ as structural Verilog: 1 circuit, main circuit main
module main (
  input  Math,
  input  Spelling,
  input  English,
  input  History,
  output Graduation
);

  wire and_1_out, or_1_out;

  and and_1 (and_1_out, Math, Spelling);
  or or_1 (or_1_out, English, History);
  or or_2 (Graduation, and_1_out, or_1_out);
endmodule
