// Logisim project Homewor3_1a.circ as structural Verilog: 1 circuit, main circuit main
// N
module main (
  input  N0,
  input  N1,
  input  N2,
  output M0,
  output M1,
  output M2,
  output M3,
  output M4
);


  assign M0 = 1'b0;
  assign M1 = 1'b0;
  assign M2 = N0;
  assign M3 = N1;
  assign M4 = N2;
endmodule
