// Logisim project Homewor3_2.circ as structural Verilog: 1 circuit, main circuit main
module main (
  input  in_1,
  input  in_2,
  input  [1:0] in_3,
  input  in_4,
  output out_5,
  output out_6
);

  wire adder_1_out, and_1_out, not_1_out, or_1_out;

  not not_1 (not_1_out, in_1);
  and and_1 (and_1_out, in_1, in_2);
  or or_1 (or_1_out, in_1, in_2);
  Adder #(.width(1)) adder_1 (.a(in_2), .b(in_1), .out(adder_1_out), .cin(in_4), .cout(out_6));
  Multiplexer #(.select(2)) multiplexer_1 (
    .in0(not_1_out), .in1(and_1_out), .in2(or_1_out), .in3(adder_1_out), .out(out_5), .sel(in_3));  // open: en
endmodule
